# Fritzing sketch disco (saved by Fritzing 0.9.3b)
breadboards: 1

parts:
  SW3 = SWITCH-MOMENTARY-2 [package=tactile-pth-12mm]
  SW2 = SWITCH-MOMENTARY-2 [package=tactile-pth-12mm]
  SW1 = SWITCH-MOMENTARY-2 [package=tactile-pth-12mm]  # not connected
  M1 = DC Motor
  713 = Motor Driver 1A Dual TB6612FNG
  3-5v = Battery Holders [package=battery-aa]
  12v = Battery Holders [package=battery-aa]
  U1 = SWITCH_SPDT [package=kps-1290]

nets (from the schematic view):
  N1: SW3.1, SW2.1, 12v.+
  N2: SW3.2, SW2.2, 713.VM
  N3: M1.pin_1, 713.A01
  N4: M1.pin_2, 713.A02
  N5: 713.GND, 3-5v.-, 12v.-
  N6: 713.PWMA, 713.STBY, 3-5v.+, U1.P
  N7: 713.AIN2, U1.S
  N8: 713.AIN1, U1.O
